# Fritzing sketch FluxCam1 (saved by Fritzing 0.9.3b)
circuit board: 7.77052cm x 5.8514cm
breadboards: 1

parts:
  U1 = LM3480IM4 [package=sot23-3]
  U2 = LM3480IM4 [package=sot23-3]
  U3 = LM3480IM4 [package=sot23-3]
  U4 = LM3480IM4 [package=sot23-3]
  U5 = LM3480IM4 [package=sot23-3]
  U6 = LM3480IM4 [package=sot23-3]
  U7 = LM3480IM4 [package=sot23-3]
  U8 = LM3480IM4 [package=sot23-3]
  U9 = LM3480IM4 [package=sot23-3]
  U10 = LM3480IM4 [package=sot23-3]
  U11 = LM3480IM4 [package=sot23-3]
  U12 = LM3480IM4 [package=sot23-3]
  U13 = LM3480IM4 [package=sot23-3]
  U14 = LM3480IM4 [package=sot23-3]
  U15 = LM3480IM4 [package=sot23-3]
  U16 = LM3480IM4 [package=sot23-3]
  U17 = LM3480IM4 [package=sot23-3]
  U18 = LM3480IM4 [package=sot23-3]
  U19 = LM3480IM4 [package=sot23-3]
  U20 = LM3480IM4 [package=sot23-3]
  U21 = LM3480IM4 [package=sot23-3]
  U22 = LM3480IM4 [package=sot23-3]
  U23 = LM3480IM4 [package=sot23-3]
  U24 = LM3480IM4 [package=sot23-3]
  U25 = LM3480IM4 [package=sot23-3]
  U26 = LM3480IM4 [package=sot23-3]
  U27 = LM3480IM4 [package=sot23-3]
  U28 = LM3480IM4 [package=sot23-3]
  U29 = LM3480IM4 [package=sot23-3]
  U30 = LM3480IM4 [package=sot23-3]
  U31 = LM3480IM4 [package=sot23-3]
  U32 = LM3480IM4 [package=sot23-3]
  U33 = LM3480IM4 [package=sot23-3]
  U34 = LM3480IM4 [package=sot23-3]
  U35 = LM3480IM4 [package=sot23-3]
  U36 = LM3480IM4 [package=sot23-3]
  U37 = LM3480IM4 [package=sot23-3]
  U38 = LM3480IM4 [package=sot23-3]
  U39 = LM3480IM4 [package=sot23-3]
  U40 = LM3480IM4 [package=sot23-3]
  U41 = LM3480IM4 [package=sot23-3]
  U42 = LM3480IM4 [package=sot23-3]
  U43 = LM3480IM4 [package=sot23-3]
  U44 = LM3480IM4 [package=sot23-3]
  U45 = LM3480IM4 [package=sot23-3]
  U46 = LM3480IM4 [package=sot23-3]
  U47 = LM3480IM4 [package=sot23-3]
  U48 = LM3480IM4 [package=sot23-3]
  U49 = LM3480IM4 [package=sot23-3]
  U50 = LM3480IM4 [package=sot23-3]
  U51 = LM3480IM4 [package=sot23-3]
  U52 = LM3480IM4 [package=sot23-3]
  U53 = LM3480IM4 [package=sot23-3]
  U54 = LM3480IM4 [package=sot23-3]
  U55 = LM3480IM4 [package=sot23-3]
  U56 = LM3480IM4 [package=sot23-3]
  U57 = LM3480IM4 [package=sot23-3]
  U58 = LM3480IM4 [package=sot23-3]
  U59 = LM3480IM4 [package=sot23-3]
  U60 = LM3480IM4 [package=sot23-3]
  U61 = LM3480IM4 [package=sot23-3]
  U62 = LM3480IM4 [package=sot23-3]
  U63 = LM3480IM4 [package=sot23-3]
  U64 = LM3480IM4 [package=sot23-3]
  Q1 = NPN-Transistor [package="TO92 [THT]"]
  Q2 = NPN-Transistor [package="TO92 [THT]"]
  Q3 = NPN-Transistor [package="TO92 [THT]"]
  Q4 = NPN-Transistor [package="TO92 [THT]"]
  Q5 = NPN-Transistor [package="TO92 [THT]"]
  Q6 = NPN-Transistor [package="TO92 [THT]"]
  Q7 = NPN-Transistor [package="TO92 [THT]"]
  Q8 = NPN-Transistor [package="TO92 [THT]"]
  J1 = female pin header, 2 pins [form="♀ (female)"]
  J2 = female pin header, 2 pins [form="♀ (female)"]
  J3 = female pin header, 2 pins [form="♀ (female)"]
  J4 = female pin header, 2 pins [form="♀ (female)"]
  J5 = female pin header, 2 pins [form="♀ (female)"]
  J6 = female pin header, 2 pins [form="♀ (female)"]
  J7 = female pin header, 2 pins [form="♀ (female)"]
  J8 = female pin header, 2 pins [form="♀ (female)"]
  R1 = Resistor [tolerance=±5% resistance=220 package=THT]
  R2 = Resistor [tolerance=±5% resistance=220 package=THT]
  R3 = Resistor [tolerance=±5% resistance=220 package=THT]
  R4 = Resistor [tolerance=±5% resistance=220 package=THT]
  R5 = Resistor [tolerance=±5% resistance=220 package=THT]
  R6 = Resistor [tolerance=±5% resistance=220 package=THT]
  R7 = Resistor [tolerance=±5% resistance=220 package=THT]
  R8 = Resistor [tolerance=±5% resistance=220 package=THT]
  J9 = female pin header, 2 pins [form="♀ (female)"]

nets:
  N1: U1.OUT, U2.OUT, U3.OUT, U4.OUT, U5.OUT, U6.OUT, U7.OUT, U8.OUT, U9.OUT, U10.OUT, U11.OUT, U12.OUT, U13.OUT, U14.OUT, U15.OUT, U16.OUT, U17.OUT, U18.OUT, U19.OUT, U20.OUT, U21.OUT, U22.OUT, U23.OUT, U24.OUT, U25.OUT, U26.OUT, U27.OUT, U28.OUT, U29.OUT, U30.OUT, U31.OUT, U32.OUT, U33.OUT, U34.OUT, U35.OUT, U36.OUT, U37.OUT, U38.OUT, U39.OUT, U40.OUT, U41.OUT, U42.OUT, U43.OUT, U44.OUT, U45.OUT, U46.OUT, U47.OUT, U48.OUT, U49.OUT, U50.OUT, U51.OUT, U52.OUT, U53.OUT, U54.OUT, U55.OUT, U56.OUT, U57.OUT, U58.OUT, U59.OUT, U60.OUT, U61.OUT, U62.OUT, U63.OUT, U64.OUT, J9.pin1
  N2: U1.IN, U9.IN, U17.IN, U25.IN, U33.IN, U41.IN, U49.IN, U57.IN, J6.pin2
  GND: U1.GND, U2.GND, U3.GND, U4.GND, U5.GND, U6.GND, U7.GND, U8.GND, Q1.C
  N3: U2.IN, U10.IN, U18.IN, U26.IN, U34.IN, U42.IN, U50.IN, U58.IN, J6.pin1
  N4: U3.IN, U11.IN, U19.IN, U27.IN, U35.IN, U43.IN, U51.IN, U59.IN, J8.pin2
  N5: U4.IN, U12.IN, U20.IN, U28.IN, U36.IN, U44.IN, U52.IN, U60.IN, J8.pin1
  N6: U5.IN, U13.IN, U21.IN, U29.IN, U37.IN, U45.IN, U53.IN, U61.IN, J7.pin2
  N7: U6.IN, U14.IN, U22.IN, U30.IN, U38.IN, U46.IN, U54.IN, U62.IN, J7.pin1
  N8: U7.IN, U15.IN, U23.IN, U31.IN, U39.IN, U47.IN, U55.IN, U63.IN, J5.pin2
  N9: U8.IN, U16.IN, U24.IN, U32.IN, U40.IN, U48.IN, U56.IN, U64.IN, J5.pin1
  GND_2: U9.GND, U10.GND, U11.GND, U12.GND, U13.GND, U14.GND, U15.GND, U16.GND, Q2.C
  GND_3: U17.GND, U18.GND, U19.GND, U20.GND, U21.GND, U22.GND, U23.GND, U24.GND, Q3.C
  GND_4: U25.GND, U26.GND, U27.GND, U28.GND, U29.GND, U30.GND, U31.GND, U32.GND, Q4.C
  GND_5: U33.GND, U34.GND, U35.GND, U36.GND, U37.GND, U38.GND, U39.GND, U40.GND, Q5.C
  GND_6: U41.GND, U42.GND, U43.GND, U44.GND, U45.GND, U46.GND, U47.GND, U48.GND, Q6.C
  GND_7: U49.GND, U50.GND, U51.GND, U52.GND, U53.GND, U54.GND, U55.GND, U56.GND, Q7.C
  GND_8: U57.GND, U58.GND, U59.GND, U60.GND, U61.GND, U62.GND, U63.GND, U64.GND, Q8.C
  N10: Q1.E, Q2.E, Q3.E, Q4.E, Q5.E, Q6.E, Q7.E, Q8.E, R1.Pin_1, R2.Pin_1, R3.Pin_1, R4.Pin_1, R5.Pin_1, R6.Pin_1, R7.Pin_1, R8.Pin_1, J9.pin2
  N11: Q1.B, J1.pin1, R8.Pin_0
  N12: Q2.B, J1.pin2, R7.Pin_0
  N13: Q3.B, J2.pin1, R6.Pin_0
  N14: Q4.B, J2.pin2, R5.Pin_0
  N15: Q5.B, J3.pin1, R4.Pin_0
  N16: Q6.B, J3.pin2, R3.Pin_0
  N17: Q7.B, J4.pin1, R2.Pin_0
  N18: Q8.B, J4.pin2, R1.Pin_0

notes:
  Output
  Row select
  FluxCam version 1 by Callum O'Riley
  +  -
  This project is Pb-free!
